# Fritzing sketch Treeduino_Arduino-Relay Interface Board (saved by Fritzing 0.6.3b)
breadboards: 1

parts:
  2n3904 = PNP-Transistor [package="TO92 [THT]"]
  10k = Resistor [tolerance=±5% resistance=10k package=THT]
  1k = Resistor [tolerance=±5% resistance=10k package=THT]
  1k1 = Resistor [tolerance=±5% resistance=10k package=THT]
  10k1 = Resistor [tolerance=±5% resistance=10k package=THT]
  Q3 = PNP-Transistor [package="TO92 [THT]"]
  1k2 = Resistor [tolerance=±5% resistance=10k package=THT]
  10k2 = Resistor [tolerance=±5% resistance=10k package=THT]
  Q4 = PNP-Transistor [package="TO92 [THT]"]
  1k3 = Resistor [tolerance=±5% resistance=10k package=THT]
  10k3 = Resistor [tolerance=±5% resistance=10k package=THT]
  Q5 = PNP-Transistor [package="TO92 [THT]"]
  1k4 = Resistor [tolerance=±5% resistance=10k package=THT]
  10k4 = Resistor [tolerance=±5% resistance=10k package=THT]
  Q6 = PNP-Transistor [package="TO92 [THT]"]
  1k5 = Resistor [tolerance=±5% resistance=10k package=THT]
  10k5 = Resistor [tolerance=±5% resistance=10k package=THT]
  Q7 = PNP-Transistor [package="TO92 [THT]"]
  1k6 = Resistor [tolerance=±5% resistance=10k package=THT]
  10k6 = Resistor [tolerance=±5% resistance=10k package=THT]
  Q8 = PNP-Transistor [package="TO92 [THT]"]
  1k7 = Resistor [tolerance=±5% resistance=10k package=THT]
  10k7 = Resistor [tolerance=±5% resistance=10k package=THT]
  +12VDC = Screw terminal - 2 pins [package=THT]
  Q2 = PNP-Transistor [package="TO92 [THT]"]
  100nF = Ceramic Capacitor [capacitance=100nF package="200 mil [THT, multilayer]"]
  100 = Resistor [tolerance=±5% resistance=220 package=THT]
  GRN = LED - 5mm [color="Red (633nm)" package="5 mm [THT]"]
  560 = Resistor [tolerance=±5% resistance=220 package=THT]
  D1 = Rectifier Diode [part_number=1N4001 package="300 mil [THT]"]
  100nF1 = Ceramic Capacitor [capacitance=100nF package="200 mil [THT, multilayer]"]
  7805 = Voltage Regulator - 5V [package="TO220 [THT]"]
  S1 = Toggle Switch [package=THT]
  part = Resistor [tolerance=±5% resistance=220 package=THT]
  LED1 = LED - 5mm [color="Red (633nm)" package="5 mm [THT]"]
  LED2 = LED - 5mm [color="Red (633nm)" package="5 mm [THT]"]

nets:
  N1: 2n3904.B, 10k.Pin_0, 1k.Pin_1
  N2: 10k.Pin_1, 10k1.Pin_1, 10k2.Pin_1, 10k3.Pin_1, 10k4.Pin_1, 10k5.Pin_1, 10k6.Pin_1, 10k7.Pin_1, +12VDC.pin1, 100nF.0, 100.Pin_1, 560.Pin_1, 100nF1.0, 7805.GND
  N3: 1k1.Pin_1, 10k1.Pin_0, Q2.B
  N4: Q3.B, 1k2.Pin_1, 10k2.Pin_0
  N5: Q4.B, 1k3.Pin_1, 10k3.Pin_0
  N6: Q5.B, 1k4.Pin_1, 10k4.Pin_0
  N7: Q6.B, 1k5.Pin_1, 10k5.Pin_0
  N8: Q7.B, 1k6.Pin_1, 10k6.Pin_0
  N9: Q8.B, 1k7.Pin_1, 10k7.Pin_0
  N10: +12VDC.pin2, D1.cathode, 100nF1.1, 7805.input_voltage, LED2.anode
  N11: 100.Pin_0, GRN.cathode
  N12: GRN.anode, D1.anode, 7805.output_voltage
  N13: 560.Pin_0, LED2.cathode
  N14: S1.COM, LED1.cathode
  N15: part.Pin_0, LED1.anode

notes:
  +12V
  +5V
  GND
